# Fritzing sketch BoardDiagram (saved by Fritzing 0.9.2b)
breadboards: 1

parts:
  ARDUINO1 = Arduino Micro
  Part1 = Digital Temperature Sensor Breakout - TMP102
  Part2 = Digital Temperature Sensor Breakout - TMP102
  Part3 = Triple Axis Magnetometer - HMC5883 Breakout
  microSD_Transflash1 = SparkFun - microSD Transflash
  Part4 = Logic Level Converter  # not connected
  Part5 = Triple Axis Gyro Breakout ITG-3200
  Part6 = Triple Axis Accelerometer Breakout - ADXL345
  BMP1 = BMP085 Breakout

nets:
  N1: ARDUINO1.D2, Part1.SDA, Part2.SDA, Part2.ADD0, Part3.SDA, Part5.SDA, Part6.SDA, BMP1.SDA
  N2: ARDUINO1.D3, Part1.SCL, Part2.SCL, Part3.SCL, Part5.SCL, Part6.SCL, BMP1.SCL
  VCC: ARDUINO1.3V3, Part1.V+, Part2.V+, Part3.VCC, microSD_Transflash1.VCC, Part5.VCC, Part6.VCC, BMP1.VIN
  GND: ARDUINO1.GND#31, Part1.GND, Part1.ADD0, Part2.GND, Part3.GND, Part5.GND, Part6.GND, BMP1.GND

custom parts:
  Arduino Micro: Arduino Micro Microcontroller
  BMP085 Breakout: A breakout for the BMP085 barometric pressure and temperature sensor
